# Fritzing sketch WispRF (saved by Fritzing 0.7.10b)

parts:
  MIRF1 = MIRF [package=mirf]  # not connected
  MIRF2 = MIRF [package=mirf]  # not connected
  S1 = Pushbutton [package=THT]
  Arduino2 = Arduino  # not connected
  J1 = Generic male header - 10 pins [package=THT]
  J2 = Generic male header - 8 pins [package=THT]
  J3 = Generic male header - 8 pins [package=THT]
  J4 = Generic male header - 6 pins [package=THT]
  J6 = Generic male header - 4 pins [package=THT]
  J5 = Generic male header - 2 pins [package=THT]
  Part1 = Arduino Prototyping Shield
  J8 = Generic female header - 8 pins [package=THT]

nets:
  N1: S1.leg0, J1.pin4, J3.pin6, J3.pin7, J6.pin4, J5.pin2, Part1.GND, Part1.N$203, Part1.N$411, Part1.N$427, J8.pin8
  N2: S1.leg1, J2.pin2, Part1.D6, Part1.N$432
  N3: J1.pin1, Part1.SCL
  N4: J1.pin2, Part1.SDA
  N5: J1.pin3, Part1.AREF
  N6: J1.pin5, Part1.D13, Part1.N$201, J8.pin4
  N7: J1.pin6, Part1.D12, Part1.N$249, J8.pin6
  N8: J1.pin7, Part1.D11, Part1.N$436, J8.pin5
  N9: J1.pin8, Part1.D10
  N10: J1.pin9, Part1.D9
  N11: J1.pin10, Part1.D8, Part1.N$434, J8.pin2
  N12: J2.pin1, Part1.D7, Part1.N$435, J8.pin3
  N13: J2.pin3, Part1.D5
  N14: J2.pin4, Part1.D4
  N15: J2.pin5, J6.pin2, Part1.D3, Part1.N$429
  N16: J2.pin6, J6.pin3, Part1.D2, Part1.N$428
  N17: J2.pin7, Part1.D1(TX)
  N18: J2.pin8, Part1.D0(RX)
  N19: J3.pin1, J3.pin2, Part1.IOREF
  N20: J3.pin3, Part1.RESET
  N21: J3.pin4, Part1.3.3V
  N22: J3.pin5, J6.pin1, J5.pin1, Part1.+5V, Part1.N$431, Part1.N$433, J8.pin1
  N23: J3.pin8, Part1.+9V
  N24: J4.pin1, Part1.A0
  N25: J4.pin2, Part1.A1
  N26: J4.pin3, Part1.A2
  N27: J4.pin4, Part1.A3
  N28: J4.pin5, Part1.A4
  N29: J4.pin6, Part1.A5
  N30: Part1.N$248, J8.pin7
